# Fritzing sketch server-with-relay (saved by Fritzing 0.9.3b)

parts:
  U1 = ESP32-38PinWide [part_number=ESP32-38PinWide]
  Switch-Manual = Toggle Switch [package=THT]
  Switch-Mode = Toggle Switch [package=THT]
  Relay = RELAY [package=relay-g5q]
  Pump = DC Motor
  220v_AC_to_5v_DC = HLK-PM01
  R1 = Resistor [tolerance=±5% resistance=220 package=THT]
  220V1 = AC Power [voltage=220 frequency=60]

nets:
  N1: U1.GPIO33, R1.Pin_0
  N2: U1.GPIO25, Switch-Manual.COM, Relay.COIL2
  N3: U1.GND, 220v_AC_to_5v_DC.-Vo
  N4: U1.VIN, Switch-Mode.L2, 220v_AC_to_5v_DC.+Vo
  N5: Switch-Manual.L2, Switch-Mode.COM, R1.Pin_1
  N6: Relay.MAIN, 220v_AC_to_5v_DC.AC#1, 220V1.V-
  N7: Relay.NO, Pump.pin_1
  N8: Pump.pin_2, 220v_AC_to_5v_DC.AC#0, 220V1.V+

custom parts:
  ESP32-38PinWide: Generic 38-Pin ESP32 with wide format (only access to one side of pins on a breadboard) based on Stephen Lilley's HiLetgo ESP-WROOM-32 ESP32 ESP-32S Development Board.
